// Logisim project ULA.circ as structural Verilog: 16 circuits, main circuit main
module main (
  input  in_1,
  input  [2:0] in_2,
  input  in_3,
  input  in_4,
  input  in_5,
  input  in_6,
  input  in_7,
  input  in_8,
  input  [4:0] in_9,
  input  [4:0] A,
  input  in_11,
  input  [4:0] B,
  input  in_13,
  input  in_14,
  input  in_15,
  input  in_16,
  input  in_17,
  input  in_18,
  input  in_19,
  input  in_20,
  input  in_21,
  output [4:0] out_22,
  output [4:0] out_23
);

  wire and_1_out, and_2_out, and_3_out, and_4_out, greater_than_1_out_6, less_or_equal_to_1_out_7,
       n5bit_comparator_1_a___b, n7_segment_decoder_1_a_2, n7_segment_decoder_1_b_2,
       n7_segment_decoder_1_c_2, n7_segment_decoder_1_d_2, n7_segment_decoder_1_e, n7_segment_decoder_1_f,
       n7_segment_decoder_1_g, n7_segment_decoder_2_a_2, n7_segment_decoder_2_b_2, n7_segment_decoder_2_c_2,
       n7_segment_decoder_2_d_2, n7_segment_decoder_2_e, n7_segment_decoder_2_f, n7_segment_decoder_2_g,
       not_1_out, not_2_out, not_3_out, or_1_out;
  wire [4:0] c2_format_1_output, greater_than_1_output, less_or_equal_to_1_output, min_1_out_6,
       n5bit_adder_1_output, n5bit_subtractor_1_output, n5bit_subtractor_2_output;

  C2_format c2_format_1 (.Input(A), .Aux(in_1), .Output(c2_format_1_output));
  greater_than greater_than_1 (
    .left_less(in_5), .left_greater(in_4), .left_equal(in_3), .out_6(greater_than_1_out_6), .A(A), .B(B),
    .Output(greater_than_1_output));
  less_or_equal_to less_or_equal_to_1 (
    .left_less(in_8), .left_greater(in_7), .left_equal(in_6), .out_7(less_or_equal_to_1_out_7), .A(A), .B(B),
    .\output (less_or_equal_to_1_output));
  min min_1 (.left_less(in_18), .left_greater(in_17), .left_equal(in_16), .A(A), .B(B), .out_6(min_1_out_6));
  _5bit_subtractor u_5bit_subtractor_1 (.\output (n5bit_subtractor_1_output), .m(in_20), .A(A), .B(B));
  _5bit_adder u_5bit_adder_1 (.\output (n5bit_adder_1_output), .m(in_21), .A(A), .B(B));
  and and_1 (and_1_out, in_2[2], not_2_out, not_1_out);
  not not_1 (not_1_out, in_2[0]);
  not not_2 (not_2_out, in_2[1]);
  and and_2 (and_2_out, greater_than_1_out_6, and_1_out);
  and and_3 (and_3_out, less_or_equal_to_1_out_7, and_4_out);
  and and_4 (and_4_out, in_2[1], in_2[0]);
  _5bit_8x1_multiplexer u_5bit_8x1_multiplexer_1 (
    .B(c2_format_1_output), .D(greater_than_1_output), .E(less_or_equal_to_1_output), .F(min_1_out_6),
    .G(n5bit_subtractor_1_output), .H(n5bit_adder_1_output), .Seletor(in_2), .out_10(out_22));  // open: A, C
  or or_1 (or_1_out, and_2_out, and_3_out);
  LED LED_STATUS (.in(or_1_out));
  _5bit_comparator u_5bit_comparator_1 (
    .left_less(in_14), .left_greater(in_13), .left_equal(in_11), .A___B(n5bit_comparator_1_a___b),
    .A(out_22), .B(in_9));  // open: A___B_2, A___B_3
  _5bit_2x1_multiplexer u_5bit_2x1_multiplexer_1 (
    .A(out_22), .B(n5bit_subtractor_2_output), .Seletor(n5bit_comparator_1_a___b), .out_4(out_23));
  not not_3 (not_3_out, n5bit_comparator_1_a___b);
  _7_segment_decoder u_7_segment_decoder_1 (
    .A(in_19), .B(in_19), .C(in_19), .D(not_3_out), .a_2(n7_segment_decoder_1_a_2),
    .b_2(n7_segment_decoder_1_b_2), .c_2(n7_segment_decoder_1_c_2), .d_2(n7_segment_decoder_1_d_2),
    .e(n7_segment_decoder_1_e), .f(n7_segment_decoder_1_f), .g(n7_segment_decoder_1_g));
  _7_Segment_Display u_7_segment_display_1 (
    .g(n7_segment_decoder_1_g), .f(n7_segment_decoder_1_f), .a(n7_segment_decoder_1_a_2),
    .b(n7_segment_decoder_1_b_2), .e(n7_segment_decoder_1_e), .d(n7_segment_decoder_1_d_2),
    .c(n7_segment_decoder_1_c_2));  // open: dp
  _5bit_subtractor u_5bit_subtractor_2 (.\output (n5bit_subtractor_2_output), .m(in_15), .A(out_22), .B(in_9));
  _7_Segment_Display u_7_segment_display_2 (
    .g(n7_segment_decoder_2_g), .f(n7_segment_decoder_2_f), .a(n7_segment_decoder_2_a_2),
    .b(n7_segment_decoder_2_b_2), .e(n7_segment_decoder_2_e), .d(n7_segment_decoder_2_d_2),
    .c(n7_segment_decoder_2_c_2));  // open: dp
  _7_segment_decoder u_7_segment_decoder_2 (
    .A(out_23[3]), .B(out_23[2]), .C(out_23[1]), .D(out_23[0]), .a_2(n7_segment_decoder_2_a_2),
    .b_2(n7_segment_decoder_2_b_2), .c_2(n7_segment_decoder_2_c_2), .d_2(n7_segment_decoder_2_d_2),
    .e(n7_segment_decoder_2_e), .f(n7_segment_decoder_2_f), .g(n7_segment_decoder_2_g));
  LED LED_NEGATIVO (.in(out_23[4]));
endmodule

module half_adder (
  input  A,
  input  B,
  output Carry_out,
  output Soma
);

  and and_1 (Carry_out, B, A);
  xor xor_1 (Soma, A, B);
endmodule

module full_adder (
  input  A,
  input  B,
  input  Carry_in,
  output Carry_out,
  output Soma
);

  wire half_adder_2_carry_out, half_adder_carry_out, half_adder_soma;

  half_adder half_adder (.A(A), .B(B), .Carry_out(half_adder_carry_out), .Soma(half_adder_soma));
  half_adder half_adder_2 (.A(half_adder_soma), .B(Carry_in), .Carry_out(half_adder_2_carry_out), .Soma(Soma));
  or or_1 (Carry_out, half_adder_carry_out, half_adder_2_carry_out);
endmodule

module C2_format (
  input  [4:0] Input,
  input  Aux,
  output [4:0] Output
);

  wire full_adder_1_carry_out, full_adder_2_carry_out, full_adder_3_carry_out, full_adder_4_carry_out,
       not_1_out, not_2_out, not_3_out, not_4_out, not_5_out, not_6_out, not_7_out, xor_1_out, xor_2_out,
       xor_3_out, xor_4_out, xor_5_out;

  not not_1 (not_1_out, Input[0]);
  not not_2 (not_2_out, Input[1]);
  not not_3 (not_3_out, Input[2]);
  not not_4 (not_4_out, Input[3]);
  not not_5 (not_5_out, Input[4]);
  not not_6 (not_6_out, Input[4]);
  not not_7 (not_7_out, not_6_out);
  xor xor_1 (xor_1_out, not_1_out, not_6_out);
  xor xor_2 (xor_2_out, not_2_out, not_6_out);
  xor xor_3 (xor_3_out, not_3_out, not_6_out);
  xor xor_4 (xor_4_out, not_4_out, not_6_out);
  xor xor_5 (xor_5_out, not_5_out, not_6_out);
  full_adder full_adder_1 (
    .A(xor_1_out), .B(not_7_out), .Carry_in(Aux), .Carry_out(full_adder_1_carry_out), .Soma(Output[0]));
  full_adder full_adder_2 (
    .A(xor_2_out), .B(Aux), .Carry_in(full_adder_1_carry_out), .Carry_out(full_adder_2_carry_out),
    .Soma(Output[1]));
  full_adder full_adder_3 (
    .A(xor_3_out), .B(Aux), .Carry_in(full_adder_2_carry_out), .Carry_out(full_adder_3_carry_out),
    .Soma(Output[2]));
  full_adder full_adder_4 (
    .A(xor_4_out), .B(Aux), .Carry_in(full_adder_3_carry_out), .Carry_out(full_adder_4_carry_out),
    .Soma(Output[3]));
  full_adder full_adder_5 (
    .A(xor_5_out), .B(Aux), .Carry_in(full_adder_4_carry_out), .Soma(Output[4]));  // open: Carry_out
endmodule

module _1bit_comparator (
  input  A,
  input  B,
  input  in_equal,
  input  in_greater_than,
  input  in_less_than,
  output A___B,
  output A___B_2,
  output A___B_3
);

  wire and_1_out, and_2_out, not_1_out, not_2_out, xnor_1_out;

  not not_1 (not_1_out, B);
  not not_2 (not_2_out, A);
  xnor xnor_1 (xnor_1_out, A, B);
  and and_1 (and_1_out, A, in_equal, not_1_out);
  and and_2 (and_2_out, not_2_out, in_equal, B);
  and and_3 (A___B, xnor_1_out, in_equal);
  or or_1 (A___B_2, in_greater_than, and_1_out);
  or or_2 (A___B_3, in_less_than, and_2_out);
endmodule

module _5bit_comparator (
  input  left_less,
  input  left_greater,
  input  left_equal,
  input  [4:0] A,
  input  [4:0] B,
  output A___B,
  output A___B_2,
  output A___B_3
);

  wire n1bit_comparator_1_a___b, n1bit_comparator_1_a___b_2, n1bit_comparator_1_a___b_3,
       n1bit_comparator_2_a___b, n1bit_comparator_2_a___b_2, n1bit_comparator_2_a___b_3,
       n1bit_comparator_3_a___b, n1bit_comparator_3_a___b_2, n1bit_comparator_3_a___b_3,
       n1bit_comparator_4_a___b, n1bit_comparator_4_a___b_2, n1bit_comparator_4_a___b_3, not_1_out, not_2_out;

  _1bit_comparator u_1bit_comparator_1 (
    .A(not_2_out), .B(not_1_out), .in_equal(left_equal), .in_greater_than(left_greater),
    .in_less_than(left_less), .A___B(n1bit_comparator_1_a___b), .A___B_2(n1bit_comparator_1_a___b_2),
    .A___B_3(n1bit_comparator_1_a___b_3));
  _1bit_comparator u_1bit_comparator_2 (
    .A(A[3]), .B(B[3]), .in_equal(n1bit_comparator_1_a___b), .in_greater_than(n1bit_comparator_1_a___b_2),
    .in_less_than(n1bit_comparator_1_a___b_3), .A___B(n1bit_comparator_2_a___b),
    .A___B_2(n1bit_comparator_2_a___b_2), .A___B_3(n1bit_comparator_2_a___b_3));
  _1bit_comparator u_1bit_comparator_3 (
    .A(A[2]), .B(B[2]), .in_equal(n1bit_comparator_2_a___b), .in_greater_than(n1bit_comparator_2_a___b_2),
    .in_less_than(n1bit_comparator_2_a___b_3), .A___B(n1bit_comparator_3_a___b),
    .A___B_2(n1bit_comparator_3_a___b_2), .A___B_3(n1bit_comparator_3_a___b_3));
  _1bit_comparator u_1bit_comparator_4 (
    .A(A[1]), .B(B[1]), .in_equal(n1bit_comparator_3_a___b), .in_greater_than(n1bit_comparator_3_a___b_2),
    .in_less_than(n1bit_comparator_3_a___b_3), .A___B(n1bit_comparator_4_a___b),
    .A___B_2(n1bit_comparator_4_a___b_2), .A___B_3(n1bit_comparator_4_a___b_3));
  not not_1 (not_1_out, B[4]);
  not not_2 (not_2_out, A[4]);
  _1bit_comparator u_1bit_comparator_5 (
    .A(A[0]), .B(B[0]), .in_equal(n1bit_comparator_4_a___b), .in_greater_than(n1bit_comparator_4_a___b_2),
    .in_less_than(n1bit_comparator_4_a___b_3), .A___B(A___B_3), .A___B_2(A___B_2), .A___B_3(A___B));
endmodule

module _5bit_adder (
  input  m,
  input  [4:0] A,
  input  [4:0] B,
  output [4:0] \output 
);

  wire full_adder_2_carry_out, full_adder_3_carry_out, full_adder_4_carry_out, full_adder_5_carry_out;

  full_adder full_adder_1 (
    .A(A[4]), .B(B[4]), .Carry_in(full_adder_2_carry_out), .Soma(\output [4]));  // open: Carry_out
  full_adder full_adder_2 (
    .A(A[3]), .B(B[3]), .Carry_in(full_adder_3_carry_out), .Carry_out(full_adder_2_carry_out),
    .Soma(\output [3]));
  full_adder full_adder_3 (
    .A(A[2]), .B(B[2]), .Carry_in(full_adder_5_carry_out), .Carry_out(full_adder_3_carry_out),
    .Soma(\output [2]));
  full_adder full_adder_4 (.A(A[0]), .B(B[0]), .Carry_in(m), .Carry_out(full_adder_4_carry_out), .Soma(\output [0]));
  full_adder full_adder_5 (
    .A(A[1]), .B(B[1]), .Carry_in(full_adder_4_carry_out), .Carry_out(full_adder_5_carry_out),
    .Soma(\output [1]));
endmodule

module _5bit_subtractor (
  input  m,
  input  [4:0] A,
  input  [4:0] B,
  output [4:0] \output 
);

  wire full_adder_1_carry_out, full_adder_3_carry_out, full_adder_4_carry_out, full_adder_5_carry_out,
       xor_1_out, xor_2_out, xor_3_out, xor_4_out, xor_5_out;

  full_adder full_adder_1 (
    .A(A[3]), .B(xor_4_out), .Carry_in(full_adder_3_carry_out), .Carry_out(full_adder_1_carry_out),
    .Soma(\output [3]));
  full_adder full_adder_2 (
    .A(A[4]), .B(xor_5_out), .Carry_in(full_adder_1_carry_out), .Soma(\output [4]));  // open: Carry_out
  full_adder full_adder_3 (
    .A(A[2]), .B(xor_3_out), .Carry_in(full_adder_5_carry_out), .Carry_out(full_adder_3_carry_out),
    .Soma(\output [2]));
  full_adder full_adder_4 (
    .A(A[0]), .B(xor_1_out), .Carry_in(m), .Carry_out(full_adder_4_carry_out), .Soma(\output [0]));
  full_adder full_adder_5 (
    .A(A[1]), .B(xor_2_out), .Carry_in(full_adder_4_carry_out), .Carry_out(full_adder_5_carry_out),
    .Soma(\output [1]));
  xor xor_1 (xor_1_out, B[0], m);
  xor xor_2 (xor_2_out, B[1], m);
  xor xor_3 (xor_3_out, B[2], m);
  xor xor_4 (xor_4_out, B[3], m);
  xor xor_5 (xor_5_out, B[4], m);
endmodule

module min (
  input  left_less,
  input  left_greater,
  input  left_equal,
  input  [4:0] A,
  input  [4:0] B,
  output [4:0] out_6
);

  wire and_1_out, n5bit_comparator_1_a___b, n5bit_comparator_1_a___b_2, n5bit_comparator_1_a___b_3,
       not_1_out, or_1_out;

  not not_1 (not_1_out, n5bit_comparator_1_a___b);
  and and_1 (and_1_out, not_1_out, or_1_out);
  _5bit_comparator u_5bit_comparator_1 (
    .left_less(left_less), .left_greater(left_greater), .left_equal(left_equal),
    .A___B(n5bit_comparator_1_a___b), .A___B_2(n5bit_comparator_1_a___b_2),
    .A___B_3(n5bit_comparator_1_a___b_3), .A(A), .B(B));
  or or_1 (or_1_out, n5bit_comparator_1_a___b_2, n5bit_comparator_1_a___b_3);
  _5bit_2x1_multiplexer u_5bit_2x1_multiplexer_1 (.A(B), .B(A), .Seletor(and_1_out), .out_4(out_6));
endmodule

module _2x1_multiplexer (
  input  A,
  input  B,
  input  Seletor,
  output out_4
);

  wire and_1_out, and_2_out, not_1_out;

  not not_1 (not_1_out, Seletor);
  and and_1 (and_1_out, A, not_1_out);
  and and_2 (and_2_out, Seletor, B);
  or or_1 (out_4, and_1_out, and_2_out);
endmodule

module _5bit_2x1_multiplexer (
  input  [4:0] A,
  input  [4:0] B,
  input  Seletor,
  output [4:0] out_4
);

  wire not_1_out;

  not not_1 (not_1_out, Seletor);
  _2x1_multiplexer u_2x1_multiplexer_1 (.A(A[0]), .B(B[0]), .Seletor(not_1_out), .out_4(out_4[0]));
  _2x1_multiplexer u_2x1_multiplexer_2 (.A(A[1]), .B(B[1]), .Seletor(not_1_out), .out_4(out_4[1]));
  _2x1_multiplexer u_2x1_multiplexer_3 (.A(A[2]), .B(B[2]), .Seletor(not_1_out), .out_4(out_4[2]));
  _2x1_multiplexer u_2x1_multiplexer_4 (.A(A[3]), .B(B[3]), .Seletor(not_1_out), .out_4(out_4[3]));
  _2x1_multiplexer u_2x1_multiplexer_5 (.A(A[4]), .B(B[4]), .Seletor(not_1_out), .out_4(out_4[4]));
endmodule

module _5bit_4x1_multiplexer (
  input  Seletor1,
  input  Seletor2,
  input  [4:0] A,
  input  [4:0] B,
  input  [4:0] C,
  input  [4:0] D,
  output [4:0] out_7
);

  wire [4:0] n5bit_2x1_multiplexer_1_out_4, n5bit_2x1_multiplexer_2_out_4;

  _5bit_2x1_multiplexer u_5bit_2x1_multiplexer_1 (
    .A(A), .B(B), .Seletor(Seletor1), .out_4(n5bit_2x1_multiplexer_1_out_4));
  _5bit_2x1_multiplexer u_5bit_2x1_multiplexer_2 (
    .A(C), .B(D), .Seletor(Seletor1), .out_4(n5bit_2x1_multiplexer_2_out_4));
  _5bit_2x1_multiplexer u_5bit_2x1_multiplexer_3 (
    .A(n5bit_2x1_multiplexer_1_out_4), .B(n5bit_2x1_multiplexer_2_out_4), .Seletor(Seletor2), .out_4(out_7));
endmodule

module _5bit_8x1_multiplexer (
  input  [2:0] Seletor,
  input  [4:0] A,
  input  [4:0] B,
  input  [4:0] C,
  input  [4:0] D,
  input  [4:0] E,
  input  [4:0] F,
  input  [4:0] G,
  input  [4:0] H,
  output [4:0] out_10
);

  wire [4:0] n5bit_4x1_multiplexer_1_out_7, n5bit_4x1_multiplexer_2_out_7;

  _5bit_4x1_multiplexer u_5bit_4x1_multiplexer_1 (
    .A(A), .B(B), .C(C), .D(D), .Seletor1(Seletor[0]), .Seletor2(Seletor[1]),
    .out_7(n5bit_4x1_multiplexer_1_out_7));
  _5bit_4x1_multiplexer u_5bit_4x1_multiplexer_2 (
    .A(E), .B(F), .C(G), .D(H), .Seletor1(Seletor[0]), .Seletor2(Seletor[1]),
    .out_7(n5bit_4x1_multiplexer_2_out_7));
  _5bit_2x1_multiplexer u_5bit_2x1_multiplexer_1 (
    .A(n5bit_4x1_multiplexer_1_out_7), .B(n5bit_4x1_multiplexer_2_out_7), .Seletor(Seletor[2]), .out_4(out_10));
endmodule

module less_or_equal_to (
  input  left_less,
  input  left_equal,
  input  left_greater,
  input  [4:0] A,
  input  [4:0] B,
  output [4:0] \output ,
  output out_7
);

  wire n5bit_comparator_1_a___b, n5bit_comparator_1_a___b_3;

  _5bit_comparator u_5bit_comparator_1 (
    .left_less(left_less), .left_greater(left_greater), .left_equal(left_equal),
    .A___B(n5bit_comparator_1_a___b), .A___B_3(n5bit_comparator_1_a___b_3), .A(A), .B(B));  // open: A___B_2
  or or_1 (out_7, n5bit_comparator_1_a___b, n5bit_comparator_1_a___b_3);

  assign \output  = A;
endmodule

module greater_than (
  input  left_less,
  input  left_equal,
  input  left_greater,
  input  [4:0] A,
  input  [4:0] B,
  output out_6,
  output [4:0] Output
);

  _5bit_comparator u_5bit_comparator_1 (
    .left_less(left_less), .left_greater(left_greater), .left_equal(left_equal), .A___B_2(out_6), .A(A), .B(B));  // open: A___B, A___B_3

  assign Output = A;
endmodule

module _7_segment_decoder (
  input  A,
  input  B,
  input  C,
  input  D,
  output a_2,
  output b_2,
  output c_2,
  output d_2,
  output e,
  output f,
  output g
);

  wire and_1_out, and_2_out, and_3_out, and_4_out, and_5_out, and_6_out, and_7_out, and_8_out, and_9_out,
       and_10_out, not_1_out, not_2_out, not_3_out, xnor_1_out, xnor_2_out, xor_1_out;

  not not_1 (not_1_out, C);
  not not_2 (not_2_out, B);
  not not_3 (not_3_out, D);
  and and_1 (and_1_out, C, not_3_out);
  and and_2 (and_2_out, not_2_out, C);
  and and_3 (and_3_out, not_2_out, not_3_out);
  and and_4 (and_4_out, B, not_1_out, D);
  and and_5 (and_5_out, C, not_3_out);
  and and_6 (and_6_out, not_2_out, not_3_out);
  and and_7 (and_7_out, not_1_out, not_3_out);
  and and_8 (and_8_out, B, not_3_out);
  and and_9 (and_9_out, B, not_1_out);
  xor xor_1 (xor_1_out, B, C);
  and and_10 (and_10_out, B, not_3_out);
  xnor xnor_1 (xnor_1_out, B, D);
  xnor xnor_2 (xnor_2_out, C, D);
  or or_1 (a_2, A, C, xnor_1_out);
  or or_2 (b_2, not_2_out, xnor_2_out);
  or or_3 (c_2, not_1_out, D, B);
  or or_4 (d_2, and_1_out, and_2_out, and_3_out, and_4_out);
  or or_5 (e, and_5_out, and_6_out);
  or or_6 (f, and_7_out, and_8_out, A, and_9_out);
  or or_7 (g, xor_1_out, A, and_10_out);
endmodule
